# Fritzing sketch inthebox_identifier (saved by Fritzing 0.9.3b)

parts:
  Composant1 = RFID-RC522-v2
  Composant2 = Arduino Uno (Rev3)

nets:
  N1: Composant1.SDA, Composant2.D10_PWM/SS
  N2: Composant1.SCK, Composant2.D13/SCK
  N3: Composant1.MOSI, Composant2.D11_PWM/MOSI
  N4: Composant1.MISO, Composant2.D12/MISO
  GND: Composant1.GND, Composant2.GND
  N5: Composant1.RST, Composant2.D9_PWM
  3.3V: Composant1.3.3V, Composant2.3V3

custom parts:
  RFID-RC522-v2: A simple China made RFID-RC522 Reader; do check the pin labels, as this is a MFRC522 based clone.
