# Fritzing sketch inthebox (saved by Fritzing 0.9.3b)
breadboards: 1

parts:
  Arduino = Arduino Uno (Rev3)
  Door_Opened_Sensor = hc-sr04
  VCC1 = Battery block 9V
  R2 = Resistor [tolerance=±5% resistance=1k package="1206 [SMD]"]
  RFID_Buzzer = Piezo Speaker
  RFID_Door_Lock = RFID-RC522-v2
  InTheBox_Weight_Sensor = MPX2010 pressure sensor [part_number=MPX]
  LED_RFID_State = RGB LED (com. cathode, rbg) [package="5 mm [THT]"]
  R3 = Resistor [tolerance=±5% resistance=1k package="1206 [SMD]"]

nets:
  N1: Arduino.A1, InTheBox_Weight_Sensor.V_out_+
  N2: Arduino.A2, InTheBox_Weight_Sensor.V_out_-
  N3: Arduino.D8, RFID_Door_Lock.MISO
  N4: Arduino.D9_PWM, RFID_Door_Lock.MOSI
  N5: Arduino.D10_PWM/SS, RFID_Door_Lock.SCK
  N6: Arduino.D11_PWM/MOSI, RFID_Door_Lock.SDA
  N7: Arduino.D12/MISO, RFID_Buzzer.pin2
  N8: Arduino.D13/SCK, R2.Pin_1
  N9: Arduino.D2, Door_Opened_Sensor.Echo
  N10: Arduino.D3_PWM, Door_Opened_Sensor.Trig
  N11: Arduino.D4, LED_RFID_State.green_anode
  N12: Arduino.D5_PWM, LED_RFID_State.blue_anode
  N13: Arduino.D6_PWM, LED_RFID_State.red_anode
  N14: Arduino.D7, RFID_Door_Lock.RST
  N15: Arduino.RESET, R2.Pin_0
  3V3: Arduino.3V3, RFID_Door_Lock.3.3V
  5V: Arduino.5V, Door_Opened_Sensor.VCC, InTheBox_Weight_Sensor.Vs
  GND: Arduino.GND, Door_Opened_Sensor.GND, VCC1.-, RFID_Buzzer.pin1, R3.Pin_0
  N16: Arduino.VIN, VCC1.+
  N17: RFID_Door_Lock.GND, LED_RFID_State.common_cathode
  N18: InTheBox_Weight_Sensor.GND, R3.Pin_1

custom parts:
  RFID-RC522-v2: A simple China made RFID-RC522 Reader; do check the pin labels, as this is a MFRC522 based clone.
