# Fritzing sketch inthebox_yun (saved by Fritzing 0.9.3b)
breadboards: 1

parts:
  Door_Opened_Sensor = hc-sr04
  VCC1 = Battery block 9V
  R2 = Resistor [tolerance=±5% resistance=1k package="1206 [SMD]"]
  RFID_Buzzer = Piezo Speaker
  RFID_Door_Lock = RFID-RC522-v2
  InTheBox_Weight_Sensor = MPX2010 pressure sensor [part_number=MPX]
  LED_RFID_State = RGB LED (com. cathode, rbg) [package="5 mm [THT]"]
  R3 = Resistor [tolerance=±5% resistance=1k package="1206 [SMD]"]
  Composant2 = Arduino Yun

nets:
  VCC: Door_Opened_Sensor.VCC, InTheBox_Weight_Sensor.Vs, Composant2.5V
  N1: Door_Opened_Sensor.Trig, Composant2.D3_PWM
  N2: Door_Opened_Sensor.Echo, Composant2.D2
  GND: Door_Opened_Sensor.GND, VCC1.-, RFID_Buzzer.pin1, R3.Pin_0, Composant2.GND
  N3: VCC1.+, Composant2.VIN
  N4: R2.Pin_0, Composant2.RESET
  N5: R2.Pin_1, Composant2.D13/SCK
  N6: RFID_Buzzer.pin2, Composant2.D12/MISO
  N7: RFID_Door_Lock.SDA, Composant2.D11_PWM/MOSI
  N8: RFID_Door_Lock.SCK, Composant2.D10_PWM/SS
  N9: RFID_Door_Lock.MOSI, Composant2.D9_PWM
  N10: RFID_Door_Lock.MISO, Composant2.D8
  N11: RFID_Door_Lock.GND, LED_RFID_State.common_cathode
  N12: RFID_Door_Lock.RST, Composant2.D7
  3.3V: RFID_Door_Lock.3.3V, Composant2.3V3
  N13: InTheBox_Weight_Sensor.GND, R3.Pin_1
  N14: InTheBox_Weight_Sensor.V_out_-, Composant2.A2
  N15: InTheBox_Weight_Sensor.V_out_+, Composant2.A1
  N16: LED_RFID_State.red_anode, Composant2.D6_PWM
  N17: LED_RFID_State.blue_anode, Composant2.D5_PWM
  N18: LED_RFID_State.green_anode, Composant2.D4

custom parts:
  RFID-RC522-v2: A simple China made RFID-RC522 Reader; do check the pin labels, as this is a MFRC522 based clone.
